# Fritzing sketch Lego 2 Axis Machine (saved by Fritzing 0.8.7b)
breadboards: 2

parts:
  Componente1 = Arduino Uno (Rev3)
  Componente2 = Arduino Uno (Rev3)
  YwRobot_Power_Supply1 = YwRobot Breadboard Power Supply [part_number=545043]
  VCC1 = Battery block 9V  # not connected
  MOTOR1 = 28BYJ-48 Stepper Motor  # not connected
  BREAKOUT1 = ULN2003A breakout board
  BREAKOUT2 = ULN2003A breakout board
  MOTOR2 = 28BYJ-48 Stepper Motor  # not connected
  DHT1 = DHT11 Humitidy and Temperature Sensor
  U1 = LCD-16X2 [package=lcd-16x2]
  LED1 = RGB LED (com. anode, rbg) [package="5 mm [THT]"]
  Componente3 = Thumb Joystick
  Componente4 = SRF05 Ultrasonic Rangefinder
  R1 = Resistor [tolerance=±5% resistance=220 package=THT]
  R2 = Resistor [tolerance=±5% resistance=220 package=THT]
  R3 = Resistor [tolerance=±5% resistance=220 package=THT]
  R4 = Resistor [tolerance=±5% resistance=220 package=THT]
  U2 = POT [package=alps_pot]
  VCC2 = Battery block 9V  # not connected

nets:
  N1: Componente1.A4/SDA, Componente2.A4/SDA
  N2: Componente1.A5/SCL, Componente2.A5/SCL
  N3: Componente1.D8, BREAKOUT1.In_1
  N4: Componente1.D9_PWM, BREAKOUT1.In_2
  N5: Componente1.D10_PWM/SS, BREAKOUT1.In_3
  N6: Componente1.D11_PWM/MOSI, BREAKOUT1.In_4
  GND: Componente1.GND, Componente2.GND, YwRobot_Power_Supply1.GND#13, YwRobot_Power_Supply1.GND#14, DHT1.GND, U1.VSS, U1.R_W, U1.K, LED1.common_anode, Componente3.GND, U2.A
  N7: Componente1.D2, Componente4.Echo
  N8: Componente1.D3_PWM, Componente4.Trig
  N9: Componente1.D4, BREAKOUT2.In_1
  N10: Componente1.D5_PWM, BREAKOUT2.In_2
  N11: Componente1.D6_PWM, BREAKOUT2.In_3
  N12: Componente1.D7, BREAKOUT2.In_4
  N13: Componente1.VIN, YwRobot_Power_Supply1.VCC#9, YwRobot_Power_Supply1.VCC#10
  N14: Componente2.A0, Componente3.VERT
  N15: Componente2.A1, Componente3.HORZ
  N16: Componente2.D8, U1.DB7
  N17: Componente2.D9_PWM, U1.DB6
  N18: Componente2.D10_PWM/SS, U1.DB5
  N19: Componente2.D11_PWM/MOSI, U1.DB4
  N20: Componente2.D12/MISO, U1.E
  N21: Componente2.D13/SCK, U1.RS
  N22: Componente2.D2, R2.Pin_0
  N23: Componente2.D3_PWM, R1.Pin_0
  N24: Componente2.D4, R3.Pin_0
  N25: Componente2.D5_PWM, DHT1.NULL
  N26: Componente2.D6_PWM, Componente3.SEL
  +5V: YwRobot_Power_Supply1.VCC#5, YwRobot_Power_Supply1.VCC#6, BREAKOUT1.+5V, BREAKOUT2.+5V, Componente4.VCC
  N27: YwRobot_Power_Supply1.GND#11, YwRobot_Power_Supply1.GND#12, BREAKOUT1.0V, BREAKOUT2.0V, Componente4.GND
  VDD: DHT1.VDD, U1.VDD, U1.A, Componente3.VCC, R4.Pin_0, U2.E
  N28: DHT1.DATA, R4.Pin_1
  N29: U1.VO, U2.S
  N30: LED1.red_cathode, R1.Pin_1
  N31: LED1.blue_cathode, R3.Pin_1
  N32: LED1.green_cathode, R2.Pin_1

notes:
  I2C Master
  I2C Slave
  Cortocircuito sui 5V (cappuccio sui 2 pin più a sinistra)
  Cortocircuito sui 12V (cappuccio sui 2 pin più a sinistra)
  Movimento asse X
  Movimento asse Y
  Per il protocollo I2C si mette in comune il riferimento GND
  Resistenze da 220 Ohm
  Resistenza da 10 KOhm

custom parts:
  YwRobot Breadboard Power Supply: The YwRobot Breadboard Power Supply (MB-V2) has two power rails; they can be 5V or 3V3. Power to the module can be provided through the female USB socket or through the A10 (female) 2.1mm power jack.
  ULN2003A breakout board: ULN2003A 7-way Darlington Transistor Driver on breakoutboard
  DHT11 Humitidy and Temperature Sensor: DHT11 Humidity and Temperature Sensor
